// Logisim project maquina_de_vendas.circ as structural Verilog: 9 circuits, main circuit main
module main (
  input  in_1,
  input  in_2,
  input  in_3,
  output out_4
);

  wire and_1_out, and_2_out, not_1_out;

  not not_1 (not_1_out, in_2);
  and and_1 (and_1_out, in_1, not_1_out);
  and and_2 (and_2_out, in_3, in_2);
  or or_1 (out_4, and_1_out, and_2_out);
endmodule

module registrador_1_bit (
  input  Set,
  input  CLK,
  input  D,
  input  CL,
  input  Load,
  output Q
);

  wire multiplexer_1_out;

  Multiplexer #(.enable("false")) multiplexer_1 (.in0(Q), .in1(D), .out(multiplexer_1_out), .sel(Load));
  D_Flip_Flop d_ff_1 (.clk(CLK), .D(multiplexer_1_out), .Q(Q), .preset(Set), .reset(CL));  // open: Qn
endmodule

module mux_1x2 (
  input  A,
  input  Sl,
  input  B,
  output Y
);

  wire and_1_out, and_2_out, not_1_out;

  not not_1 (not_1_out, Sl);
  and and_1 (and_1_out, A, not_1_out);
  and and_2 (and_2_out, B, Sl);
  or or_1 (Y, and_1_out, and_2_out);
endmodule

module registrador_4_bits (
  input  D0,
  input  D1,
  input  Clk,
  input  D2,
  input  Set,
  input  D3,
  input  CL,
  input  Load,
  output Q0,
  output Q1,
  output Q2,
  output Q3
);

  registrador_1_bit registrador_1_bit_1 (.Set(Set), .CLK(Clk), .D(D0), .Load(Load), .CL(CL), .Q(Q0));
  registrador_1_bit registrador_1_bit_2 (.Set(Set), .CLK(Clk), .D(D1), .Load(Load), .CL(CL), .Q(Q1));
  registrador_1_bit registrador_1_bit_3 (.Set(Set), .CLK(Clk), .D(D2), .Load(Load), .CL(CL), .Q(Q2));
  registrador_1_bit registrador_1_bit_4 (.Set(Set), .CLK(Clk), .D(D3), .Load(Load), .CL(CL), .Q(Q3));
endmodule

module somador_4_bits (
  input  C_in,
  input  A0,
  input  B0,
  input  A1,
  input  B1,
  input  A2,
  input  B2,
  input  A3,
  input  B3,
  output S0,
  output S1,
  output S2,
  output S3,
  output C0
);

  wire somador_1_bit_1_c_out, somador_1_bit_2_c_out, somador_1_bit_3_c_out;

  somador_1_bit somador_1_bit_1 (.B(B0), .C_in(C_in), .S(S0), .C_out(somador_1_bit_1_c_out), .A(A0));
  somador_1_bit somador_1_bit_2 (.B(B1), .C_in(somador_1_bit_1_c_out), .S(S1), .C_out(somador_1_bit_2_c_out), .A(A1));
  somador_1_bit somador_1_bit_3 (.B(B2), .C_in(somador_1_bit_2_c_out), .S(S2), .C_out(somador_1_bit_3_c_out), .A(A2));
  somador_1_bit somador_1_bit_4 (.B(B3), .C_in(somador_1_bit_3_c_out), .S(S3), .C_out(C0), .A(A3));
endmodule

module somador_1_bit (
  input  A,
  input  B,
  input  C_in,
  output S,
  output C_out
);

  wire and_1_out, and_2_out, and_3_out, and_4_out, not_1_out, xnor_1_out, xor_1_out;

  xnor xnor_1 (xnor_1_out, A, B);
  xor xor_1 (xor_1_out, A, B);
  and and_1 (and_1_out, xnor_1_out, C_in);
  not not_1 (not_1_out, C_in);
  and and_2 (and_2_out, not_1_out, xor_1_out);
  and and_3 (and_3_out, xor_1_out, C_in);
  and and_4 (and_4_out, A, B);
  or or_1 (S, and_1_out, and_2_out);
  or or_2 (C_out, and_3_out, and_4_out);
endmodule

module datapath (
  input  Vm0,
  input  Vm1,
  input  Vm2,
  input  Vm3,
  input  Vd0,
  input  Vd1,
  input  Vd2,
  input  Vd3,
  input  CLK,
  input  Ld,
  input  CL,
  output me
);

  wire clock_1_out, registrador_4_bits_2_q0, registrador_4_bits_2_q1, registrador_4_bits_2_q2,
       registrador_4_bits_2_q3, registrador_4_bits_3_q0, registrador_4_bits_3_q1, registrador_4_bits_3_q2,
       registrador_4_bits_3_q3;
  wire [3:0] registrador_4_bits_1_q0, somador_4_bits_1_s0;
  wire [7:0] bit_extender_1_out, bit_extender_2_out;

  Clock clock_1 (.out(clock_1_out));
  registrador_4_bits registrador_4_bits_1 (
    .D0(Vd0), .D1(Vd1), .Clk(clock_1_out), .D2(Vd2), .Set(1'b0), .D3(Vd3), .Q0(registrador_4_bits_1_q0[0]),
    .Q1(registrador_4_bits_1_q0[1]), .Q2(registrador_4_bits_1_q0[2]), .Q3(registrador_4_bits_1_q0[3]),
    .Load(1'b1), .CL(1'b0));
  assign bit_extender_1_out = {{4{1'b0}}, registrador_4_bits_1_q0};  // Bit_Extender bit_extender_1
  assign bit_extender_2_out = {{4{1'b0}}, somador_4_bits_1_s0};  // Bit_Extender bit_extender_2
  Comparator #(.mode("unsigned")) comparator_1 (
    .a(bit_extender_2_out), .b(bit_extender_1_out), .lt(me));  // open: gt, eq
  registrador_4_bits registrador_4_bits_2 (
    .D0(Vm0), .D1(Vm1), .Clk(clock_1_out), .D2(Vm2), .Set(1'b0), .D3(Vm3), .Q0(registrador_4_bits_2_q0),
    .Q1(registrador_4_bits_2_q1), .Q2(registrador_4_bits_2_q2), .Q3(registrador_4_bits_2_q3), .Load(1'b1),
    .CL(1'b0));
  registrador_4_bits registrador_4_bits_3 (
    .D0(somador_4_bits_1_s0[0]), .D1(somador_4_bits_1_s0[1]), .Clk(clock_1_out), .D2(somador_4_bits_1_s0[2]),
    .Set(1'b0), .D3(somador_4_bits_1_s0[3]), .Q0(registrador_4_bits_3_q0), .Q1(registrador_4_bits_3_q1),
    .Q2(registrador_4_bits_3_q2), .Q3(registrador_4_bits_3_q3), .Load(Ld), .CL(CL));
  somador_4_bits somador_4_bits_1 (
    .A0(registrador_4_bits_3_q0), .B0(registrador_4_bits_2_q0), .A1(registrador_4_bits_3_q1),
    .B1(registrador_4_bits_2_q1), .A2(registrador_4_bits_3_q2), .B2(registrador_4_bits_2_q2),
    .A3(registrador_4_bits_3_q3), .B3(registrador_4_bits_2_q3), .S0(somador_4_bits_1_s0[0]),
    .S1(somador_4_bits_1_s0[1]), .S2(somador_4_bits_1_s0[2]), .S3(somador_4_bits_1_s0[3]), .C_in(1'b0));  // open: C0
endmodule

module controller (
  input  C,
  input  CLK,
  input  me,
  output Ld,
  output d,
  output CL,
  output S1,
  output S0
);

  wire and_1_out, and_5_out, and_6_out, d_ff_1_qn, d_ff_2_qn, not_1_out, not_2_out, or_1_out, or_2_out;

  D_Flip_Flop d_ff_1 (.clk(CLK), .D(and_6_out), .Q(S1), .Qn(d_ff_1_qn), .preset(1'b0), .reset(1'b0));
  D_Flip_Flop d_ff_2 (.clk(CLK), .D(or_1_out), .Q(S0), .Qn(d_ff_2_qn), .preset(1'b0), .reset(1'b0));
  not not_1 (not_1_out, C);
  and and_1 (and_1_out, not_1_out, d_ff_1_qn);
  or or_1 (or_1_out, and_1_out, d_ff_2_qn);
  not not_2 (not_2_out, me);
  and and_2 (Ld, S1, d_ff_2_qn);
  and and_3 (d, S1, S0);
  and and_4 (CL, d_ff_1_qn, d_ff_2_qn);
  and and_5 (and_5_out, d_ff_1_qn, S0);
  or or_2 (or_2_out, C, not_2_out);
  and and_6 (and_6_out, and_5_out, or_2_out);
endmodule

module maquina_de_vendas (
  input  C,
  input  Vd0,
  input  Vd1,
  input  Vd2,
  input  Vd3,
  input  Vm0,
  input  Vm1,
  input  Vm2,
  input  Vm3,
  output d
);

  wire clock_1_out, controller_1_cl, controller_1_ld, datapath_1_me;

  controller controller_1 (
    .C(C), .me(datapath_1_me), .Ld(controller_1_ld), .d(d), .CL(controller_1_cl), .CLK(clock_1_out));  // open: S1, S0
  Clock clock_1 (.out(clock_1_out));
  datapath datapath_1 (
    .Ld(controller_1_ld), .me(datapath_1_me), .Vd0(Vd0), .Vd1(Vd1), .Vd2(Vd2), .Vd3(Vd3), .Vm0(Vm0),
    .Vm1(Vm1), .Vm2(Vm2), .Vm3(Vm3), .CL(controller_1_cl), .CLK(clock_1_out));
endmodule
