// Logisim project FIFO.circ as structural Verilog: 12 circuits, main circuit main
module main (
  input  in_1,
  input  in_2,
  input  in_3,
  output out_4
);

  wire and_1_out, and_2_out, not_1_out;

  not not_1 (not_1_out, in_2);
  and and_1 (and_1_out, in_1, not_1_out);
  and and_2 (and_2_out, in_3, in_2);
  or or_1 (out_4, and_1_out, and_2_out);
endmodule

module registrador_1_bit (
  input  Set,
  input  CLK,
  input  D,
  input  CL,
  input  Load,
  output Q
);

  wire multiplexer_1_out;

  Multiplexer #(.enable("false")) multiplexer_1 (.in0(Q), .in1(D), .out(multiplexer_1_out), .sel(Load));
  D_Flip_Flop d_ff_1 (.clk(CLK), .D(multiplexer_1_out), .Q(Q), .preset(Set), .reset(CL));  // open: Qn
endmodule

module mux_1x2 (
  input  A,
  input  Sl,
  input  B,
  output Y
);

  wire and_1_out, and_2_out, not_1_out;

  not not_1 (not_1_out, Sl);
  and and_1 (and_1_out, A, not_1_out);
  and and_2 (and_2_out, B, Sl);
  or or_1 (Y, and_1_out, and_2_out);
endmodule

module registrador_4_bits (
  input  D0,
  input  D1,
  input  Clk,
  input  D2,
  input  Set,
  input  D3,
  input  CL,
  input  Load,
  output Q0,
  output Q1,
  output Q2,
  output Q3
);

  registrador_1_bit registrador_1_bit_1 (.Set(Set), .CLK(Clk), .D(D0), .Load(Load), .CL(CL), .Q(Q0));
  registrador_1_bit registrador_1_bit_2 (.Set(Set), .CLK(Clk), .D(D1), .Load(Load), .CL(CL), .Q(Q1));
  registrador_1_bit registrador_1_bit_3 (.Set(Set), .CLK(Clk), .D(D2), .Load(Load), .CL(CL), .Q(Q2));
  registrador_1_bit registrador_1_bit_4 (.Set(Set), .CLK(Clk), .D(D3), .Load(Load), .CL(CL), .Q(Q3));
endmodule

module somador_4_bits (
  input  C_in,
  input  A0,
  input  B0,
  input  A1,
  input  B1,
  input  A2,
  input  B2,
  input  A3,
  input  B3,
  output S0,
  output S1,
  output S2,
  output S3,
  output C0
);

  wire somador_1_bit_1_c_out, somador_1_bit_2_c_out, somador_1_bit_3_c_out;

  somador_1_bit somador_1_bit_1 (.B(B0), .C_in(C_in), .S(S0), .C_out(somador_1_bit_1_c_out), .A(A0));
  somador_1_bit somador_1_bit_2 (.B(B1), .C_in(somador_1_bit_1_c_out), .S(S1), .C_out(somador_1_bit_2_c_out), .A(A1));
  somador_1_bit somador_1_bit_3 (.B(B2), .C_in(somador_1_bit_2_c_out), .S(S2), .C_out(somador_1_bit_3_c_out), .A(A2));
  somador_1_bit somador_1_bit_4 (.B(B3), .C_in(somador_1_bit_3_c_out), .S(S3), .C_out(C0), .A(A3));
endmodule

module somador_1_bit (
  input  A,
  input  B,
  input  C_in,
  output S,
  output C_out
);

  wire and_1_out, and_2_out, and_3_out, and_4_out, not_1_out, xnor_1_out, xor_1_out;

  xnor xnor_1 (xnor_1_out, A, B);
  xor xor_1 (xor_1_out, A, B);
  and and_1 (and_1_out, xnor_1_out, C_in);
  not not_1 (not_1_out, C_in);
  and and_2 (and_2_out, not_1_out, xor_1_out);
  and and_3 (and_3_out, xor_1_out, C_in);
  and and_4 (and_4_out, A, B);
  or or_1 (S, and_1_out, and_2_out);
  or or_2 (C_out, and_3_out, and_4_out);
endmodule

module B_reg (
  input  addr_w0,
  input  addr_w1,
  input  clk,
  input  clr,
  input  w_0,
  input  w_1,
  input  w_2,
  input  w_3,
  input  addr_w2,
  input  en_wr,
  input  addr_r0,
  input  addr_r1,
  input  addr_r2,
  input  en_rd,
  output r_0,
  output r_1,
  output r_2,
  output r_3
);

  wire d_0, d_1, d_2, d_3, d_4, d_5, d_6, d_7, mux_1x8_1_out_12, mux_1x8_2_out_12, mux_1x8_3_out_12,
       mux_1x8_4_out_12, registrador_4_bits_1_q0, registrador_4_bits_1_q1, registrador_4_bits_1_q2,
       registrador_4_bits_1_q3, registrador_4_bits_2_q0, registrador_4_bits_2_q1, registrador_4_bits_2_q2,
       registrador_4_bits_2_q3, registrador_4_bits_3_q0, registrador_4_bits_3_q1, registrador_4_bits_3_q2,
       registrador_4_bits_3_q3, registrador_4_bits_4_q0, registrador_4_bits_4_q1, registrador_4_bits_4_q2,
       registrador_4_bits_4_q3, registrador_4_bits_5_q0, registrador_4_bits_5_q1, registrador_4_bits_5_q2,
       registrador_4_bits_5_q3, registrador_4_bits_6_q0, registrador_4_bits_6_q1, registrador_4_bits_6_q2,
       registrador_4_bits_6_q3, registrador_4_bits_7_q0, registrador_4_bits_7_q1, registrador_4_bits_7_q2,
       registrador_4_bits_7_q3, registrador_4_bits_9_q0, registrador_4_bits_9_q1, registrador_4_bits_9_q2,
       registrador_4_bits_9_q3;

  registrador_4_bits registrador_4_bits_1 (
    .D0(w_0), .D1(w_1), .Clk(clk), .D2(w_2), .Set(1'b0), .D3(w_3), .Q0(registrador_4_bits_1_q0),
    .Q1(registrador_4_bits_1_q1), .Q2(registrador_4_bits_1_q2), .Q3(registrador_4_bits_1_q3), .Load(d_0),
    .CL(clr));
  registrador_4_bits registrador_4_bits_2 (
    .D0(w_0), .D1(w_1), .Clk(clk), .D2(w_2), .Set(1'b0), .D3(w_3), .Q0(registrador_4_bits_2_q0),
    .Q1(registrador_4_bits_2_q1), .Q2(registrador_4_bits_2_q2), .Q3(registrador_4_bits_2_q3), .Load(d_1),
    .CL(clr));
  registrador_4_bits registrador_4_bits_3 (
    .D0(w_0), .D1(w_1), .Clk(clk), .D2(w_2), .Set(1'b0), .D3(w_3), .Q0(registrador_4_bits_3_q0),
    .Q1(registrador_4_bits_3_q1), .Q2(registrador_4_bits_3_q2), .Q3(registrador_4_bits_3_q3), .Load(d_2),
    .CL(clr));
  decoder_3x8 decoder_3x8_1 (
    .s_0(addr_w0), .s_1(addr_w1), .s_2(addr_w2), .en(en_wr), .d_0(d_0), .d_1(d_1), .d_2(d_2), .d_3(d_3),
    .d_4(d_4), .d_5(d_5), .d_6(d_6), .d_7(d_7));
  registrador_4_bits registrador_4_bits_4 (
    .D0(w_0), .D1(w_1), .Clk(clk), .D2(w_2), .Set(1'b0), .D3(w_3), .Q0(registrador_4_bits_4_q0),
    .Q1(registrador_4_bits_4_q1), .Q2(registrador_4_bits_4_q2), .Q3(registrador_4_bits_4_q3), .Load(d_3),
    .CL(clr));
  mux_1x8 mux_1x8_1 (
    .A(registrador_4_bits_1_q0), .B(registrador_4_bits_2_q0), .C(registrador_4_bits_3_q0),
    .D(registrador_4_bits_4_q0), .E(registrador_4_bits_5_q0), .F(registrador_4_bits_6_q0),
    .G(registrador_4_bits_7_q0), .H(registrador_4_bits_9_q0), .out_12(mux_1x8_1_out_12), .S_0(addr_r0),
    .S_1(addr_r1), .S_2(addr_r2));
  registrador_4_bits registrador_4_bits_5 (
    .D0(w_0), .D1(w_1), .Clk(clk), .D2(w_2), .Set(1'b0), .D3(w_3), .Q0(registrador_4_bits_5_q0),
    .Q1(registrador_4_bits_5_q1), .Q2(registrador_4_bits_5_q2), .Q3(registrador_4_bits_5_q3), .Load(d_4),
    .CL(clr));
  registrador_4_bits registrador_4_bits_6 (
    .D0(w_0), .D1(w_1), .Clk(clk), .D2(w_2), .Set(1'b0), .D3(w_3), .Q0(registrador_4_bits_6_q0),
    .Q1(registrador_4_bits_6_q1), .Q2(registrador_4_bits_6_q2), .Q3(registrador_4_bits_6_q3), .Load(d_5),
    .CL(clr));
  mux_1x8 mux_1x8_2 (
    .A(registrador_4_bits_1_q1), .B(registrador_4_bits_2_q1), .C(registrador_4_bits_3_q1),
    .D(registrador_4_bits_4_q1), .E(registrador_4_bits_5_q1), .F(registrador_4_bits_6_q1),
    .G(registrador_4_bits_7_q1), .H(registrador_4_bits_9_q1), .out_12(mux_1x8_2_out_12), .S_0(addr_r0),
    .S_1(addr_r1), .S_2(addr_r2));
  registrador_4_bits registrador_4_bits_7 (
    .D0(w_0), .D1(w_1), .Clk(clk), .D2(w_2), .Set(1'b0), .D3(w_3), .Q0(registrador_4_bits_7_q0),
    .Q1(registrador_4_bits_7_q1), .Q2(registrador_4_bits_7_q2), .Q3(registrador_4_bits_7_q3), .Load(d_6),
    .CL(clr));
  registrador_4_bits registrador_4_bits_8 (
    .D0(mux_1x8_1_out_12), .D1(mux_1x8_2_out_12), .Clk(clk), .D2(mux_1x8_3_out_12), .Set(1'b0),
    .D3(mux_1x8_4_out_12), .Q0(r_0), .Q1(r_1), .Q2(r_2), .Q3(r_3), .Load(en_rd), .CL(clr));
  registrador_4_bits registrador_4_bits_9 (
    .D0(w_0), .D1(w_1), .Clk(clk), .D2(w_2), .Set(1'b0), .D3(w_3), .Q0(registrador_4_bits_9_q0),
    .Q1(registrador_4_bits_9_q1), .Q2(registrador_4_bits_9_q2), .Q3(registrador_4_bits_9_q3), .Load(d_7),
    .CL(clr));
  mux_1x8 mux_1x8_3 (
    .A(registrador_4_bits_1_q2), .B(registrador_4_bits_2_q2), .C(registrador_4_bits_3_q2),
    .D(registrador_4_bits_4_q2), .E(registrador_4_bits_5_q2), .F(registrador_4_bits_6_q2),
    .G(registrador_4_bits_7_q2), .H(registrador_4_bits_9_q2), .out_12(mux_1x8_3_out_12), .S_0(addr_r0),
    .S_1(addr_r1), .S_2(addr_r2));
  mux_1x8 mux_1x8_4 (
    .A(registrador_4_bits_1_q3), .B(registrador_4_bits_2_q3), .C(registrador_4_bits_3_q3),
    .D(registrador_4_bits_4_q3), .E(registrador_4_bits_5_q3), .F(registrador_4_bits_6_q3),
    .G(registrador_4_bits_7_q3), .H(registrador_4_bits_9_q3), .out_12(mux_1x8_4_out_12), .S_0(addr_r0),
    .S_1(addr_r1), .S_2(addr_r2));

  // Other names for the same wires on the sheet: ck = clk; cl = clr
endmodule

module mux_1x4 (
  input  S_0,
  input  A,
  input  S_1,
  input  B,
  input  C,
  input  D,
  output Y_4
);

  wire mux_1x2_1_y, mux_1x2_2_y;

  mux_1x2 mux_1x2_1 (.A(A), .Sl(S_0), .B(B), .Y(mux_1x2_1_y));
  mux_1x2 mux_1x2_2 (.A(C), .Sl(S_0), .B(D), .Y(mux_1x2_2_y));
  mux_1x2 mux_1x2_3 (.A(mux_1x2_1_y), .Sl(S_1), .B(mux_1x2_2_y), .Y(Y_4));
endmodule

module mux_1x8 (
  input  S_0,
  input  S_1,
  input  A,
  input  S_2,
  input  B,
  input  C,
  input  D,
  input  E,
  input  F,
  input  G,
  input  H,
  output out_12
);

  wire mux_1x4_1_y_4, mux_1x4_2_y_4;

  mux_1x4 mux_1x4_1 (.A(A), .B(B), .C(C), .D(D), .Y_4(mux_1x4_1_y_4), .S_0(S_0), .S_1(S_1));
  mux_1x4 mux_1x4_2 (.A(E), .B(F), .C(G), .D(H), .Y_4(mux_1x4_2_y_4), .S_0(S_0), .S_1(S_1));
  mux_1x2 mux_1x2_1 (.A(mux_1x4_1_y_4), .Sl(S_2), .B(mux_1x4_2_y_4), .Y(out_12));
endmodule

module decoder_3x8 (
  input  s_0,
  input  s_1,
  input  s_2,
  input  en,
  output d_0,
  output d_1,
  output d_2,
  output d_3,
  output d_4,
  output d_5,
  output d_6,
  output d_7
);

  wire and_1_out, and_2_out, and_3_out, and_4_out, and_5_out, and_6_out, not_1_out, not_2_out, not_3_out;

  not not_1 (not_1_out, s_0);
  not not_2 (not_2_out, s_1);
  not not_3 (not_3_out, s_2);
  and and_1 (and_1_out, not_1_out, not_2_out);
  and and_2 (and_2_out, not_1_out, s_1);
  and and_3 (and_3_out, not_3_out, en);
  and and_4 (and_4_out, s_2, en);
  and and_5 (and_5_out, not_2_out, s_0);
  and and_6 (and_6_out, s_0, s_1);
  and and_7 (d_0, and_1_out, and_3_out);
  and and_8 (d_1, and_5_out, and_3_out);
  and and_9 (d_2, and_2_out, and_3_out);
  and and_10 (d_3, and_6_out, and_3_out);
  and and_11 (d_4, and_1_out, and_4_out);
  and and_12 (d_5, and_5_out, and_4_out);
  and and_13 (d_6, and_2_out, and_4_out);
  and and_14 (d_7, and_6_out, and_4_out);
endmodule

module contador (
  input  clk,
  input  cnt,
  input  clr,
  output c2,
  output c_1,
  output c_0
);

  wire somador_4_bits_1_s0, somador_4_bits_1_s1, somador_4_bits_1_s2;

  registrador_4_bits registrador_4_bits_1 (
    .D0(1'b0), .D1(somador_4_bits_1_s2), .Clk(clk), .D2(somador_4_bits_1_s1), .Set(1'b0),
    .D3(somador_4_bits_1_s0), .Q1(c2), .Q2(c_1), .Q3(c_0), .Load(cnt), .CL(clr));  // open: Q0
  somador_4_bits somador_4_bits_1 (
    .A0(c_0), .B0(1'b0), .A1(c_1), .B1(1'b0), .A2(c2), .B2(1'b0), .S0(somador_4_bits_1_s0),
    .S1(somador_4_bits_1_s1), .S2(somador_4_bits_1_s2), .C_in(1'b1));  // open: A3, B3, S3, C0
endmodule

module FIFO (
  input  clr,
  input  w3,
  input  w2,
  input  w1,
  input  w0,
  input  rd,
  input  wr
);

  wire ADDR_R_c2, ADDR_R_c_0, ADDR_R_c_1, ADDR_W_c2, ADDR_W_c_0, ADDR_W_c_1, ck;
  wire [3:0] b_reg_1_r_3;

  contador ADDR_R (.clr(clr), .cnt(rd), .c_1(ADDR_R_c_1), .c_0(ADDR_R_c_0), .c2(ADDR_R_c2), .clk(ck));
  B_reg b_reg_1 (
    .addr_w0(ADDR_W_c_0), .addr_w1(ADDR_W_c_1), .clr(clr), .addr_w2(ADDR_W_c2), .addr_r0(ADDR_R_c_0),
    .addr_r1(ADDR_R_c_1), .addr_r2(ADDR_R_c2), .en_rd(rd), .w_0(w3), .w_1(w2), .w_2(w1), .w_3(w0),
    .en_wr(wr), .r_0(b_reg_1_r_3[3]), .r_1(b_reg_1_r_3[2]), .r_2(b_reg_1_r_3[1]), .r_3(b_reg_1_r_3[0]),
    .clk(ck));
  Clock clock_1 (.out(ck));
  contador ADDR_W (.clr(clr), .cnt(wr), .c_1(ADDR_W_c_1), .c_0(ADDR_W_c_0), .c2(ADDR_W_c2), .clk(ck));
  Hex_Digit_Display hex_digit_display_1 (.value(b_reg_1_r_3));  // open: dp
endmodule
